# Fritzing sketch led_grid (saved by Fritzing 0.9.3b)
circuit board: 20cm x 15cm
breadboards: 1

parts:
  RGB_SMD_LED1 = SMD RGB LED (WS2812) [package=5050]
  RGB_SMD_LED18 = SMD RGB LED (WS2812) [package=5050]
  RGB_SMD_LED29 = SMD RGB LED (WS2812) [package=5050]
  RGB_SMD_LED32 = SMD RGB LED (WS2812) [package=5050]
  RGB_SMD_LED24 = SMD RGB LED (WS2812) [package=5050]
  RGB_SMD_LED22 = SMD RGB LED (WS2812) [package=5050]
  RGB_SMD_LED4 = SMD RGB LED (WS2812) [package=5050]
  RGB_SMD_LED6 = SMD RGB LED (WS2812) [package=5050]
  RGB_SMD_LED26 = SMD RGB LED (WS2812) [package=5050]
  RGB_SMD_LED3 = SMD RGB LED (WS2812) [package=5050]
  RGB_SMD_LED13 = SMD RGB LED (WS2812) [package=5050]
  RGB_SMD_LED16 = SMD RGB LED (WS2812) [package=5050]
  RGB_SMD_LED9 = SMD RGB LED (WS2812) [package=5050]
  RGB_SMD_LED12 = SMD RGB LED (WS2812) [package=5050]
  RGB_SMD_LED2 = SMD RGB LED (WS2812) [package=5050]
  RGB_SMD_LED17 = SMD RGB LED (WS2812) [package=5050]
  RGB_SMD_LED28 = SMD RGB LED (WS2812) [package=5050]
  RGB_SMD_LED14 = SMD RGB LED (WS2812) [package=5050]
  RGB_SMD_LED11 = SMD RGB LED (WS2812) [package=5050]
  RGB_SMD_LED23 = SMD RGB LED (WS2812) [package=5050]
  RGB_SMD_LED7 = SMD RGB LED (WS2812) [package=5050]
  RGB_SMD_LED20 = SMD RGB LED (WS2812) [package=5050]
  RGB_SMD_LED31 = SMD RGB LED (WS2812) [package=5050]
  RGB_SMD_LED21 = SMD RGB LED (WS2812) [package=5050]
  RGB_SMD_LED8 = SMD RGB LED (WS2812) [package=5050]
  RGB_SMD_LED25 = SMD RGB LED (WS2812) [package=5050]
  RGB_SMD_LED15 = SMD RGB LED (WS2812) [package=5050]
  RGB_SMD_LED5 = SMD RGB LED (WS2812) [package=5050]
  RGB_SMD_LED10 = SMD RGB LED (WS2812) [package=5050]
  RGB_SMD_LED27 = SMD RGB LED (WS2812) [package=5050]
  RGB_SMD_LED30 = SMD RGB LED (WS2812) [package=5050]
  RGB_SMD_LED19 = SMD RGB LED (WS2812) [package=5050]
  RGB_SMD_LED33 = SMD RGB LED (WS2812) [package=5050]
  RGB_SMD_LED34 = SMD RGB LED (WS2812) [package=5050]
  RGB_SMD_LED35 = SMD RGB LED (WS2812) [package=5050]
  RGB_SMD_LED36 = SMD RGB LED (WS2812) [package=5050]
  RGB_SMD_LED37 = SMD RGB LED (WS2812) [package=5050]
  RGB_SMD_LED38 = SMD RGB LED (WS2812) [package=5050]
  RGB_SMD_LED39 = SMD RGB LED (WS2812) [package=5050]
  RGB_SMD_LED40 = SMD RGB LED (WS2812) [package=5050]
  RGB_SMD_LED41 = SMD RGB LED (WS2812) [package=5050]
  RGB_SMD_LED42 = SMD RGB LED (WS2812) [package=5050]
  RGB_SMD_LED43 = SMD RGB LED (WS2812) [package=5050]
  RGB_SMD_LED44 = SMD RGB LED (WS2812) [package=5050]
  RGB_SMD_LED45 = SMD RGB LED (WS2812) [package=5050]
  RGB_SMD_LED46 = SMD RGB LED (WS2812) [package=5050]
  RGB_SMD_LED47 = SMD RGB LED (WS2812) [package=5050]
  RGB_SMD_LED48 = SMD RGB LED (WS2812) [package=5050]
  RGB_SMD_LED49 = SMD RGB LED (WS2812) [package=5050]
  RGB_SMD_LED50 = SMD RGB LED (WS2812) [package=5050]
  RGB_SMD_LED51 = SMD RGB LED (WS2812) [package=5050]
  RGB_SMD_LED52 = SMD RGB LED (WS2812) [package=5050]
  RGB_SMD_LED53 = SMD RGB LED (WS2812) [package=5050]
  RGB_SMD_LED54 = SMD RGB LED (WS2812) [package=5050]
  RGB_SMD_LED55 = SMD RGB LED (WS2812) [package=5050]
  RGB_SMD_LED56 = SMD RGB LED (WS2812) [package=5050]
  RGB_SMD_LED57 = SMD RGB LED (WS2812) [package=5050]
  RGB_SMD_LED58 = SMD RGB LED (WS2812) [package=5050]
  RGB_SMD_LED59 = SMD RGB LED (WS2812) [package=5050]
  RGB_SMD_LED60 = SMD RGB LED (WS2812) [package=5050]
  RGB_SMD_LED61 = SMD RGB LED (WS2812) [package=5050]
  RGB_SMD_LED62 = SMD RGB LED (WS2812) [package=5050]
  RGB_SMD_LED63 = SMD RGB LED (WS2812) [package=5050]
  RGB_SMD_LED64 = SMD RGB LED (WS2812) [package=5050]
  RGB_SMD_LED65 = SMD RGB LED (WS2812) [package=5050]
  RGB_SMD_LED66 = SMD RGB LED (WS2812) [package=5050]
  RGB_SMD_LED67 = SMD RGB LED (WS2812) [package=5050]
  RGB_SMD_LED68 = SMD RGB LED (WS2812) [package=5050]
  RGB_SMD_LED69 = SMD RGB LED (WS2812) [package=5050]
  RGB_SMD_LED70 = SMD RGB LED (WS2812) [package=5050]
  RGB_SMD_LED71 = SMD RGB LED (WS2812) [package=5050]
  RGB_SMD_LED72 = SMD RGB LED (WS2812) [package=5050]
  RGB_SMD_LED73 = SMD RGB LED (WS2812) [package=5050]
  RGB_SMD_LED74 = SMD RGB LED (WS2812) [package=5050]
  RGB_SMD_LED75 = SMD RGB LED (WS2812) [package=5050]
  RGB_SMD_LED76 = SMD RGB LED (WS2812) [package=5050]
  RGB_SMD_LED77 = SMD RGB LED (WS2812) [package=5050]
  RGB_SMD_LED78 = SMD RGB LED (WS2812) [package=5050]
  RGB_SMD_LED79 = SMD RGB LED (WS2812) [package=5050]
  RGB_SMD_LED80 = SMD RGB LED (WS2812) [package=5050]
  RGB_SMD_LED81 = SMD RGB LED (WS2812) [package=5050]
  RGB_SMD_LED82 = SMD RGB LED (WS2812) [package=5050]
  RGB_SMD_LED83 = SMD RGB LED (WS2812) [package=5050]
  RGB_SMD_LED84 = SMD RGB LED (WS2812) [package=5050]
  RGB_SMD_LED85 = SMD RGB LED (WS2812) [package=5050]
  RGB_SMD_LED86 = SMD RGB LED (WS2812) [package=5050]
  RGB_SMD_LED87 = SMD RGB LED (WS2812) [package=5050]
  RGB_SMD_LED88 = SMD RGB LED (WS2812) [package=5050]
  RGB_SMD_LED89 = SMD RGB LED (WS2812) [package=5050]
  RGB_SMD_LED90 = SMD RGB LED (WS2812) [package=5050]
  RGB_SMD_LED91 = SMD RGB LED (WS2812) [package=5050]
  RGB_SMD_LED92 = SMD RGB LED (WS2812) [package=5050]
  RGB_SMD_LED93 = SMD RGB LED (WS2812) [package=5050]
  RGB_SMD_LED94 = SMD RGB LED (WS2812) [package=5050]
  RGB_SMD_LED95 = SMD RGB LED (WS2812) [package=5050]
  RGB_SMD_LED96 = SMD RGB LED (WS2812) [package=5050]
  RGB_SMD_LED97 = SMD RGB LED (WS2812) [package=5050]
  RGB_SMD_LED98 = SMD RGB LED (WS2812) [package=5050]
  RGB_SMD_LED99 = SMD RGB LED (WS2812) [package=5050]
  RGB_SMD_LED100 = SMD RGB LED (WS2812) [package=5050]
  RGB_SMD_LED101 = SMD RGB LED (WS2812) [package=5050]
  RGB_SMD_LED102 = SMD RGB LED (WS2812) [package=5050]
  RGB_SMD_LED103 = SMD RGB LED (WS2812) [package=5050]
  RGB_SMD_LED104 = SMD RGB LED (WS2812) [package=5050]
  RGB_SMD_LED105 = SMD RGB LED (WS2812) [package=5050]
  RGB_SMD_LED106 = SMD RGB LED (WS2812) [package=5050]
  RGB_SMD_LED107 = SMD RGB LED (WS2812) [package=5050]
  RGB_SMD_LED108 = SMD RGB LED (WS2812) [package=5050]
  RGB_SMD_LED109 = SMD RGB LED (WS2812) [package=5050]
  RGB_SMD_LED110 = SMD RGB LED (WS2812) [package=5050]
  RGB_SMD_LED111 = SMD RGB LED (WS2812) [package=5050]
  RGB_SMD_LED112 = SMD RGB LED (WS2812) [package=5050]
  RGB_SMD_LED113 = SMD RGB LED (WS2812) [package=5050]
  RGB_SMD_LED114 = SMD RGB LED (WS2812) [package=5050]
  RGB_SMD_LED115 = SMD RGB LED (WS2812) [package=5050]
  RGB_SMD_LED116 = SMD RGB LED (WS2812) [package=5050]
  RGB_SMD_LED117 = SMD RGB LED (WS2812) [package=5050]
  RGB_SMD_LED118 = SMD RGB LED (WS2812) [package=5050]
  RGB_SMD_LED119 = SMD RGB LED (WS2812) [package=5050]
  RGB_SMD_LED120 = SMD RGB LED (WS2812) [package=5050]
  RGB_SMD_LED121 = SMD RGB LED (WS2812) [package=5050]
  RGB_SMD_LED122 = SMD RGB LED (WS2812) [package=5050]
  RGB_SMD_LED123 = SMD RGB LED (WS2812) [package=5050]
  RGB_SMD_LED124 = SMD RGB LED (WS2812) [package=5050]
  RGB_SMD_LED125 = SMD RGB LED (WS2812) [package=5050]
  RGB_SMD_LED126 = SMD RGB LED (WS2812) [package=5050]
  RGB_SMD_LED127 = SMD RGB LED (WS2812) [package=5050]
  RGB_SMD_LED128 = SMD RGB LED (WS2812) [package=5050]
  RGB_SMD_LED129 = SMD RGB LED (WS2812) [package=5050]
  RGB_SMD_LED130 = SMD RGB LED (WS2812) [package=5050]
  RGB_SMD_LED131 = SMD RGB LED (WS2812) [package=5050]
  RGB_SMD_LED132 = SMD RGB LED (WS2812) [package=5050]
  RGB_SMD_LED133 = SMD RGB LED (WS2812) [package=5050]
  RGB_SMD_LED134 = SMD RGB LED (WS2812) [package=5050]
  RGB_SMD_LED135 = SMD RGB LED (WS2812) [package=5050]
  RGB_SMD_LED136 = SMD RGB LED (WS2812) [package=5050]
  RGB_SMD_LED137 = SMD RGB LED (WS2812) [package=5050]
  RGB_SMD_LED138 = SMD RGB LED (WS2812) [package=5050]
  RGB_SMD_LED139 = SMD RGB LED (WS2812) [package=5050]
  RGB_SMD_LED140 = SMD RGB LED (WS2812) [package=5050]
  RGB_SMD_LED141 = SMD RGB LED (WS2812) [package=5050]
  RGB_SMD_LED142 = SMD RGB LED (WS2812) [package=5050]
  RGB_SMD_LED143 = SMD RGB LED (WS2812) [package=5050]
  RGB_SMD_LED144 = SMD RGB LED (WS2812) [package=5050]
  RGB_SMD_LED145 = SMD RGB LED (WS2812) [package=5050]
  RGB_SMD_LED146 = SMD RGB LED (WS2812) [package=5050]
  RGB_SMD_LED147 = SMD RGB LED (WS2812) [package=5050]
  RGB_SMD_LED148 = SMD RGB LED (WS2812) [package=5050]
  RGB_SMD_LED149 = SMD RGB LED (WS2812) [package=5050]
  RGB_SMD_LED150 = SMD RGB LED (WS2812) [package=5050]
  RGB_SMD_LED151 = SMD RGB LED (WS2812) [package=5050]
  RGB_SMD_LED152 = SMD RGB LED (WS2812) [package=5050]
  RGB_SMD_LED153 = SMD RGB LED (WS2812) [package=5050]
  RGB_SMD_LED154 = SMD RGB LED (WS2812) [package=5050]
  RGB_SMD_LED155 = SMD RGB LED (WS2812) [package=5050]
  RGB_SMD_LED156 = SMD RGB LED (WS2812) [package=5050]
  RGB_SMD_LED157 = SMD RGB LED (WS2812) [package=5050]
  RGB_SMD_LED158 = SMD RGB LED (WS2812) [package=5050]
  RGB_SMD_LED159 = SMD RGB LED (WS2812) [package=5050]
  RGB_SMD_LED160 = SMD RGB LED (WS2812) [package=5050]
  RGB_SMD_LED161 = SMD RGB LED (WS2812) [package=5050]
  RGB_SMD_LED162 = SMD RGB LED (WS2812) [package=5050]
  RGB_SMD_LED163 = SMD RGB LED (WS2812) [package=5050]
  RGB_SMD_LED164 = SMD RGB LED (WS2812) [package=5050]
  RGB_SMD_LED165 = SMD RGB LED (WS2812) [package=5050]
  RGB_SMD_LED166 = SMD RGB LED (WS2812) [package=5050]
  RGB_SMD_LED167 = SMD RGB LED (WS2812) [package=5050]
  RGB_SMD_LED168 = SMD RGB LED (WS2812) [package=5050]
  RGB_SMD_LED169 = SMD RGB LED (WS2812) [package=5050]
  RGB_SMD_LED170 = SMD RGB LED (WS2812) [package=5050]
  RGB_SMD_LED171 = SMD RGB LED (WS2812) [package=5050]
  RGB_SMD_LED172 = SMD RGB LED (WS2812) [package=5050]
  RGB_SMD_LED173 = SMD RGB LED (WS2812) [package=5050]
  RGB_SMD_LED174 = SMD RGB LED (WS2812) [package=5050]
  RGB_SMD_LED175 = SMD RGB LED (WS2812) [package=5050]
  RGB_SMD_LED176 = SMD RGB LED (WS2812) [package=5050]
  Q1 = TRANSISTOR_NPN [package=sot23-3]
  Q2 = TRANSISTOR_NPN [package=sot23-3]
  Q3 = TRANSISTOR_NPN [package=sot23-3]
  Q4 = TRANSISTOR_NPN [package=sot23-3]
  Q5 = TRANSISTOR_NPN [package=sot23-3]
  Q6 = TRANSISTOR_NPN [package=sot23-3]
  Q7 = TRANSISTOR_NPN [package=sot23-3]
  Q8 = TRANSISTOR_NPN [package=sot23-3]
  Q9 = TRANSISTOR_NPN [package=sot23-3]
  Q10 = TRANSISTOR_NPN [package=sot23-3]
  Q11 = TRANSISTOR_NPN [package=sot23-3]
  ATMega328 = atmega328 [package=dip]
  MCP7940M_Addr_0xDE = IC, DIP package, 8 pins [chip_label=MCP7940M]
  PCA9956B_Addr_0x32 = TSSOP20 [chip_label=IC package=TSSOP]
  PCA9956B_Addr_0x2A = TSSOP20 [chip_label=IC package=TSSOP]
  C3 = Capacitor [package=cap-pth-small2]
  XTAL_32_768kHz = Crystal [package=SMD]
  C2 = Capacitor [package=0805]
  C1 = Capacitor [package=0805]
  S1 = Square Pushbutton
  S2 = Square Pushbutton
  R7_10kOhm = Resistor [tolerance=±5% resistance=220 package=THT]
  R8_10kOhm = Resistor [tolerance=±5% resistance=220 package=THT]
  R5_3kOhm = Resistor [tolerance=±5% resistance=220 package="1206 [SMD]"]
  R6_10kOhm = Resistor [tolerance=±5% resistance=220 package="1206 [SMD]"]
  R3_3kOhm = Resistor [tolerance=±5% resistance=220 package="1206 [SMD]"]
  R4_10kOhm = Resistor [tolerance=±5% resistance=220 package="1206 [SMD]"]
  R1_10kOhm = Resistor [tolerance=±5% resistance=220 package="1206 [SMD]"]
  R2_10kOhm = Resistor [tolerance=±5% resistance=220 package="1206 [SMD]"]
  C5_0_1uF = Capacitor [package=cap-pth-large]
  C4_0_1uF = Capacitor [package=cap-pth-large]
  X1 = USB Connectors [package=usb-microb]
  S3 = Square Pushbutton
  D1 = Diode [package=diode-1n4148]
  +_Batt_- = Header 2 [package=jst-2-pth]

nets:
  N1: RGB_SMD_LED1.DOut, RGB_SMD_LED18.DOut, PCA9956B_Addr_0x32.LED0
  N2: RGB_SMD_LED1.DIn, RGB_SMD_LED18.DIn, PCA9956B_Addr_0x32.LED1
  VCC: RGB_SMD_LED1.VCC, RGB_SMD_LED18.VCC, PCA9956B_Addr_0x32.LED2
  VDD: RGB_SMD_LED1.NC, RGB_SMD_LED1.VDD, RGB_SMD_LED1.VSS, RGB_SMD_LED4.NC, RGB_SMD_LED4.VDD, RGB_SMD_LED4.VSS, RGB_SMD_LED6.NC, RGB_SMD_LED6.VDD, RGB_SMD_LED6.VSS, RGB_SMD_LED3.NC, RGB_SMD_LED3.VDD, RGB_SMD_LED3.VSS, RGB_SMD_LED13.NC, RGB_SMD_LED13.VDD, RGB_SMD_LED13.VSS, RGB_SMD_LED16.NC, RGB_SMD_LED16.VDD, RGB_SMD_LED16.VSS, RGB_SMD_LED9.NC, RGB_SMD_LED9.VDD, RGB_SMD_LED9.VSS, RGB_SMD_LED12.NC, RGB_SMD_LED12.VDD, RGB_SMD_LED12.VSS, RGB_SMD_LED2.NC, RGB_SMD_LED2.VDD, RGB_SMD_LED2.VSS, RGB_SMD_LED14.NC, RGB_SMD_LED14.VDD, RGB_SMD_LED14.VSS, RGB_SMD_LED11.NC, RGB_SMD_LED11.VDD, RGB_SMD_LED11.VSS, RGB_SMD_LED7.NC, RGB_SMD_LED7.VDD, RGB_SMD_LED7.VSS, RGB_SMD_LED8.NC, RGB_SMD_LED8.VDD, RGB_SMD_LED8.VSS, RGB_SMD_LED15.NC, RGB_SMD_LED15.VDD, RGB_SMD_LED15.VSS, RGB_SMD_LED5.NC, RGB_SMD_LED5.VDD, RGB_SMD_LED5.VSS, RGB_SMD_LED10.NC, RGB_SMD_LED10.VDD, RGB_SMD_LED10.VSS, Q1.E
  VDD_2: RGB_SMD_LED18.NC, RGB_SMD_LED18.VDD, RGB_SMD_LED18.VSS, RGB_SMD_LED29.NC, RGB_SMD_LED29.VDD, RGB_SMD_LED29.VSS, RGB_SMD_LED32.NC, RGB_SMD_LED32.VDD, RGB_SMD_LED32.VSS, RGB_SMD_LED24.NC, RGB_SMD_LED24.VDD, RGB_SMD_LED24.VSS, RGB_SMD_LED22.NC, RGB_SMD_LED22.VDD, RGB_SMD_LED22.VSS, RGB_SMD_LED26.NC, RGB_SMD_LED26.VDD, RGB_SMD_LED26.VSS, RGB_SMD_LED17.NC, RGB_SMD_LED17.VDD, RGB_SMD_LED17.VSS, RGB_SMD_LED28.NC, RGB_SMD_LED28.VDD, RGB_SMD_LED28.VSS, RGB_SMD_LED23.NC, RGB_SMD_LED23.VDD, RGB_SMD_LED23.VSS, RGB_SMD_LED20.NC, RGB_SMD_LED20.VDD, RGB_SMD_LED20.VSS, RGB_SMD_LED31.NC, RGB_SMD_LED31.VDD, RGB_SMD_LED31.VSS, RGB_SMD_LED21.NC, RGB_SMD_LED21.VDD, RGB_SMD_LED21.VSS, RGB_SMD_LED25.NC, RGB_SMD_LED25.VDD, RGB_SMD_LED25.VSS, RGB_SMD_LED27.NC, RGB_SMD_LED27.VDD, RGB_SMD_LED27.VSS, RGB_SMD_LED30.NC, RGB_SMD_LED30.VDD, RGB_SMD_LED30.VSS, RGB_SMD_LED19.NC, RGB_SMD_LED19.VDD, RGB_SMD_LED19.VSS, Q11.E
  N3: RGB_SMD_LED29.DOut, RGB_SMD_LED15.DOut, PCA9956B_Addr_0x2A.LED18
  N4: RGB_SMD_LED29.DIn, RGB_SMD_LED15.DIn, PCA9956B_Addr_0x2A.LED19
  VCC_2: RGB_SMD_LED29.VCC, RGB_SMD_LED15.VCC, PCA9956B_Addr_0x2A.LED20
  N5: RGB_SMD_LED32.DOut, RGB_SMD_LED8.DOut, PCA9956B_Addr_0x32.LED21
  N6: RGB_SMD_LED32.DIn, RGB_SMD_LED8.DIn, PCA9956B_Addr_0x32.LED22
  VCC_3: RGB_SMD_LED32.VCC, RGB_SMD_LED8.VCC, PCA9956B_Addr_0x32.LED23
  N7: RGB_SMD_LED24.DOut, RGB_SMD_LED4.DOut, PCA9956B_Addr_0x32.LED9
  N8: RGB_SMD_LED24.DIn, RGB_SMD_LED4.DIn, PCA9956B_Addr_0x32.LED10
  VCC_4: RGB_SMD_LED24.VCC, RGB_SMD_LED4.VCC, PCA9956B_Addr_0x32.LED11
  N9: RGB_SMD_LED22.DOut, RGB_SMD_LED11.DOut, PCA9956B_Addr_0x2A.LED6
  N10: RGB_SMD_LED22.DIn, RGB_SMD_LED11.DIn, PCA9956B_Addr_0x2A.LED7
  VCC_5: RGB_SMD_LED22.VCC, RGB_SMD_LED11.VCC, PCA9956B_Addr_0x2A.LED8
  N11: RGB_SMD_LED6.DOut, RGB_SMD_LED28.DOut, PCA9956B_Addr_0x32.LED15
  N12: RGB_SMD_LED6.DIn, RGB_SMD_LED28.DIn, PCA9956B_Addr_0x32.LED16
  VCC_6: RGB_SMD_LED6.VCC, RGB_SMD_LED28.VCC, PCA9956B_Addr_0x32.LED17
  N13: RGB_SMD_LED26.DOut, RGB_SMD_LED13.DOut, PCA9956B_Addr_0x2A.LED12
  N14: RGB_SMD_LED26.DIn, RGB_SMD_LED13.DIn, PCA9956B_Addr_0x2A.LED13
  VCC_7: RGB_SMD_LED26.VCC, RGB_SMD_LED13.VCC, PCA9956B_Addr_0x2A.LED14
  N15: RGB_SMD_LED3.DOut, RGB_SMD_LED21.DOut, PCA9956B_Addr_0x32.LED6
  N16: RGB_SMD_LED3.DIn, RGB_SMD_LED21.DIn, PCA9956B_Addr_0x32.LED7
  VCC_8: RGB_SMD_LED3.VCC, RGB_SMD_LED21.VCC, PCA9956B_Addr_0x32.LED8
  N17: RGB_SMD_LED16.DOut, RGB_SMD_LED31.DOut, PCA9956B_Addr_0x2A.LED21
  N18: RGB_SMD_LED16.DIn, RGB_SMD_LED31.DIn, PCA9956B_Addr_0x2A.LED22
  VCC_9: RGB_SMD_LED16.VCC, RGB_SMD_LED31.VCC, PCA9956B_Addr_0x2A.LED23
  N19: RGB_SMD_LED9.DOut, RGB_SMD_LED17.DOut, PCA9956B_Addr_0x2A.LED0
  N20: RGB_SMD_LED9.DIn, RGB_SMD_LED17.DIn, PCA9956B_Addr_0x2A.LED1
  VCC_10: RGB_SMD_LED9.VCC, RGB_SMD_LED17.VCC, PCA9956B_Addr_0x2A.LED2
  N21: RGB_SMD_LED12.DOut, RGB_SMD_LED23.DOut, PCA9956B_Addr_0x2A.LED9
  N22: RGB_SMD_LED12.DIn, RGB_SMD_LED23.DIn, PCA9956B_Addr_0x2A.LED10
  VCC_11: RGB_SMD_LED12.VCC, RGB_SMD_LED23.VCC, PCA9956B_Addr_0x2A.LED11
  N23: RGB_SMD_LED2.DOut, RGB_SMD_LED20.DOut, PCA9956B_Addr_0x32.LED3
  N24: RGB_SMD_LED2.DIn, RGB_SMD_LED20.DIn, PCA9956B_Addr_0x32.LED4
  VCC_12: RGB_SMD_LED2.VCC, RGB_SMD_LED20.VCC, PCA9956B_Addr_0x32.LED5
  N25: RGB_SMD_LED14.DOut, RGB_SMD_LED27.DOut, PCA9956B_Addr_0x2A.LED15
  N26: RGB_SMD_LED14.DIn, RGB_SMD_LED27.DIn, PCA9956B_Addr_0x2A.LED16
  VCC_13: RGB_SMD_LED14.VCC, RGB_SMD_LED27.VCC, PCA9956B_Addr_0x2A.LED17
  N27: RGB_SMD_LED7.DOut, RGB_SMD_LED30.DOut, PCA9956B_Addr_0x32.LED18
  N28: RGB_SMD_LED7.DIn, RGB_SMD_LED30.DIn, PCA9956B_Addr_0x32.LED19
  VCC_14: RGB_SMD_LED7.VCC, RGB_SMD_LED30.VCC, PCA9956B_Addr_0x32.LED20
  N29: RGB_SMD_LED25.DOut, RGB_SMD_LED5.DOut, PCA9956B_Addr_0x32.LED12
  N30: RGB_SMD_LED25.DIn, RGB_SMD_LED5.DIn, PCA9956B_Addr_0x32.LED13
  VCC_15: RGB_SMD_LED25.VCC, RGB_SMD_LED5.VCC, PCA9956B_Addr_0x32.LED14
  N31: RGB_SMD_LED10.DOut, RGB_SMD_LED19.DOut, PCA9956B_Addr_0x2A.LED3
  N32: RGB_SMD_LED10.DIn, RGB_SMD_LED19.DIn, PCA9956B_Addr_0x2A.LED4
  VCC_16: RGB_SMD_LED10.VCC, RGB_SMD_LED19.VCC, PCA9956B_Addr_0x2A.LED5
  N33: RGB_SMD_LED33.DOut, RGB_SMD_LED36.DOut
  N34: RGB_SMD_LED33.DIn, RGB_SMD_LED36.DIn
  VCC_17: RGB_SMD_LED33.VCC, RGB_SMD_LED36.VCC
  VDD_3: RGB_SMD_LED33.NC, RGB_SMD_LED33.VDD, RGB_SMD_LED33.VSS, RGB_SMD_LED34.NC, RGB_SMD_LED34.VDD, RGB_SMD_LED34.VSS, RGB_SMD_LED37.NC, RGB_SMD_LED37.VDD, RGB_SMD_LED37.VSS, RGB_SMD_LED39.NC, RGB_SMD_LED39.VDD, RGB_SMD_LED39.VSS, RGB_SMD_LED41.NC, RGB_SMD_LED41.VDD, RGB_SMD_LED41.VSS, RGB_SMD_LED43.NC, RGB_SMD_LED43.VDD, RGB_SMD_LED43.VSS, RGB_SMD_LED45.NC, RGB_SMD_LED45.VDD, RGB_SMD_LED45.VSS, RGB_SMD_LED48.NC, RGB_SMD_LED48.VDD, RGB_SMD_LED48.VSS, RGB_SMD_LED50.NC, RGB_SMD_LED50.VDD, RGB_SMD_LED50.VSS, RGB_SMD_LED52.NC, RGB_SMD_LED52.VDD, RGB_SMD_LED52.VSS, RGB_SMD_LED53.NC, RGB_SMD_LED53.VDD, RGB_SMD_LED53.VSS, RGB_SMD_LED55.NC, RGB_SMD_LED55.VDD, RGB_SMD_LED55.VSS, RGB_SMD_LED57.NC, RGB_SMD_LED57.VDD, RGB_SMD_LED57.VSS, RGB_SMD_LED60.NC, RGB_SMD_LED60.VDD, RGB_SMD_LED60.VSS, RGB_SMD_LED62.NC, RGB_SMD_LED62.VDD, RGB_SMD_LED62.VSS, RGB_SMD_LED64.NC, RGB_SMD_LED64.VDD, RGB_SMD_LED64.VSS, Q3.E
  N35: RGB_SMD_LED34.DOut, RGB_SMD_LED35.DOut
  N36: RGB_SMD_LED34.DIn, RGB_SMD_LED35.DIn
  VCC_18: RGB_SMD_LED34.VCC, RGB_SMD_LED35.VCC
  VDD_4: RGB_SMD_LED35.NC, RGB_SMD_LED35.VDD, RGB_SMD_LED35.VSS, RGB_SMD_LED36.NC, RGB_SMD_LED36.VDD, RGB_SMD_LED36.VSS, RGB_SMD_LED38.NC, RGB_SMD_LED38.VDD, RGB_SMD_LED38.VSS, RGB_SMD_LED40.NC, RGB_SMD_LED40.VDD, RGB_SMD_LED40.VSS, RGB_SMD_LED42.NC, RGB_SMD_LED42.VDD, RGB_SMD_LED42.VSS, RGB_SMD_LED44.NC, RGB_SMD_LED44.VDD, RGB_SMD_LED44.VSS, RGB_SMD_LED46.NC, RGB_SMD_LED46.VDD, RGB_SMD_LED46.VSS, RGB_SMD_LED47.NC, RGB_SMD_LED47.VDD, RGB_SMD_LED47.VSS, RGB_SMD_LED49.NC, RGB_SMD_LED49.VDD, RGB_SMD_LED49.VSS, RGB_SMD_LED51.NC, RGB_SMD_LED51.VDD, RGB_SMD_LED51.VSS, RGB_SMD_LED54.NC, RGB_SMD_LED54.VDD, RGB_SMD_LED54.VSS, RGB_SMD_LED56.NC, RGB_SMD_LED56.VDD, RGB_SMD_LED56.VSS, RGB_SMD_LED58.NC, RGB_SMD_LED58.VDD, RGB_SMD_LED58.VSS, RGB_SMD_LED59.NC, RGB_SMD_LED59.VDD, RGB_SMD_LED59.VSS, RGB_SMD_LED61.NC, RGB_SMD_LED61.VDD, RGB_SMD_LED61.VSS, RGB_SMD_LED63.NC, RGB_SMD_LED63.VDD, RGB_SMD_LED63.VSS, Q2.E
  N37: RGB_SMD_LED37.DOut, RGB_SMD_LED38.DOut
  N38: RGB_SMD_LED37.DIn, RGB_SMD_LED38.DIn
  VCC_19: RGB_SMD_LED37.VCC, RGB_SMD_LED38.VCC
  N39: RGB_SMD_LED39.DOut, RGB_SMD_LED40.DOut
  N40: RGB_SMD_LED39.DIn, RGB_SMD_LED40.DIn
  VCC_20: RGB_SMD_LED39.VCC, RGB_SMD_LED40.VCC
  N41: RGB_SMD_LED41.DOut, RGB_SMD_LED44.DOut
  N42: RGB_SMD_LED41.DIn, RGB_SMD_LED44.DIn
  VCC_21: RGB_SMD_LED41.VCC, RGB_SMD_LED44.VCC
  N43: RGB_SMD_LED42.DOut, RGB_SMD_LED43.DOut
  N44: RGB_SMD_LED42.DIn, RGB_SMD_LED43.DIn
  VCC_22: RGB_SMD_LED42.VCC, RGB_SMD_LED43.VCC
  N45: RGB_SMD_LED45.DOut, RGB_SMD_LED46.DOut
  N46: RGB_SMD_LED45.DIn, RGB_SMD_LED46.DIn
  VCC_23: RGB_SMD_LED45.VCC, RGB_SMD_LED46.VCC
  N47: RGB_SMD_LED47.DOut, RGB_SMD_LED48.DOut
  N48: RGB_SMD_LED47.DIn, RGB_SMD_LED48.DIn
  VCC_24: RGB_SMD_LED47.VCC, RGB_SMD_LED48.VCC
  N49: RGB_SMD_LED49.DOut, RGB_SMD_LED50.DOut
  N50: RGB_SMD_LED49.DIn, RGB_SMD_LED50.DIn
  VCC_25: RGB_SMD_LED49.VCC, RGB_SMD_LED50.VCC
  N51: RGB_SMD_LED51.DOut, RGB_SMD_LED52.DOut
  N52: RGB_SMD_LED51.DIn, RGB_SMD_LED52.DIn
  VCC_26: RGB_SMD_LED51.VCC, RGB_SMD_LED52.VCC
  N53: RGB_SMD_LED53.DOut, RGB_SMD_LED54.DOut
  N54: RGB_SMD_LED53.DIn, RGB_SMD_LED54.DIn
  VCC_27: RGB_SMD_LED53.VCC, RGB_SMD_LED54.VCC
  N55: RGB_SMD_LED55.DOut, RGB_SMD_LED56.DOut
  N56: RGB_SMD_LED55.DIn, RGB_SMD_LED56.DIn
  VCC_28: RGB_SMD_LED55.VCC, RGB_SMD_LED56.VCC
  N57: RGB_SMD_LED57.DOut, RGB_SMD_LED59.DOut
  N58: RGB_SMD_LED57.DIn, RGB_SMD_LED59.DIn
  VCC_29: RGB_SMD_LED57.VCC, RGB_SMD_LED59.VCC
  N59: RGB_SMD_LED58.DOut, RGB_SMD_LED60.DOut
  N60: RGB_SMD_LED58.DIn, RGB_SMD_LED60.DIn
  VCC_30: RGB_SMD_LED58.VCC, RGB_SMD_LED60.VCC
  N61: RGB_SMD_LED61.DOut, RGB_SMD_LED64.DOut
  N62: RGB_SMD_LED61.DIn, RGB_SMD_LED64.DIn
  VCC_31: RGB_SMD_LED61.VCC, RGB_SMD_LED64.VCC
  N63: RGB_SMD_LED62.DOut, RGB_SMD_LED63.DOut
  N64: RGB_SMD_LED62.DIn, RGB_SMD_LED63.DIn
  VCC_32: RGB_SMD_LED62.VCC, RGB_SMD_LED63.VCC
  N65: RGB_SMD_LED65.DOut, RGB_SMD_LED68.DOut
  N66: RGB_SMD_LED65.DIn, RGB_SMD_LED68.DIn
  VCC_33: RGB_SMD_LED65.VCC, RGB_SMD_LED68.VCC
  VDD_5: RGB_SMD_LED65.NC, RGB_SMD_LED65.VDD, RGB_SMD_LED65.VSS, RGB_SMD_LED66.NC, RGB_SMD_LED66.VDD, RGB_SMD_LED66.VSS, RGB_SMD_LED69.NC, RGB_SMD_LED69.VDD, RGB_SMD_LED69.VSS, RGB_SMD_LED71.NC, RGB_SMD_LED71.VDD, RGB_SMD_LED71.VSS, RGB_SMD_LED73.NC, RGB_SMD_LED73.VDD, RGB_SMD_LED73.VSS, RGB_SMD_LED75.NC, RGB_SMD_LED75.VDD, RGB_SMD_LED75.VSS, RGB_SMD_LED77.NC, RGB_SMD_LED77.VDD, RGB_SMD_LED77.VSS, RGB_SMD_LED80.NC, RGB_SMD_LED80.VDD, RGB_SMD_LED80.VSS, RGB_SMD_LED82.NC, RGB_SMD_LED82.VDD, RGB_SMD_LED82.VSS, RGB_SMD_LED84.NC, RGB_SMD_LED84.VDD, RGB_SMD_LED84.VSS, RGB_SMD_LED85.NC, RGB_SMD_LED85.VDD, RGB_SMD_LED85.VSS, RGB_SMD_LED87.NC, RGB_SMD_LED87.VDD, RGB_SMD_LED87.VSS, RGB_SMD_LED89.NC, RGB_SMD_LED89.VDD, RGB_SMD_LED89.VSS, RGB_SMD_LED92.NC, RGB_SMD_LED92.VDD, RGB_SMD_LED92.VSS, RGB_SMD_LED94.NC, RGB_SMD_LED94.VDD, RGB_SMD_LED94.VSS, RGB_SMD_LED96.NC, RGB_SMD_LED96.VDD, RGB_SMD_LED96.VSS, Q5.E
  N67: RGB_SMD_LED66.DOut, RGB_SMD_LED67.DOut
  N68: RGB_SMD_LED66.DIn, RGB_SMD_LED67.DIn
  VCC_34: RGB_SMD_LED66.VCC, RGB_SMD_LED67.VCC
  VDD_6: RGB_SMD_LED67.NC, RGB_SMD_LED67.VDD, RGB_SMD_LED67.VSS, RGB_SMD_LED68.NC, RGB_SMD_LED68.VDD, RGB_SMD_LED68.VSS, RGB_SMD_LED70.NC, RGB_SMD_LED70.VDD, RGB_SMD_LED70.VSS, RGB_SMD_LED72.NC, RGB_SMD_LED72.VDD, RGB_SMD_LED72.VSS, RGB_SMD_LED74.NC, RGB_SMD_LED74.VDD, RGB_SMD_LED74.VSS, RGB_SMD_LED76.NC, RGB_SMD_LED76.VDD, RGB_SMD_LED76.VSS, RGB_SMD_LED78.NC, RGB_SMD_LED78.VDD, RGB_SMD_LED78.VSS, RGB_SMD_LED79.NC, RGB_SMD_LED79.VDD, RGB_SMD_LED79.VSS, RGB_SMD_LED81.NC, RGB_SMD_LED81.VDD, RGB_SMD_LED81.VSS, RGB_SMD_LED83.NC, RGB_SMD_LED83.VDD, RGB_SMD_LED83.VSS, RGB_SMD_LED86.NC, RGB_SMD_LED86.VDD, RGB_SMD_LED86.VSS, RGB_SMD_LED88.NC, RGB_SMD_LED88.VDD, RGB_SMD_LED88.VSS, RGB_SMD_LED90.NC, RGB_SMD_LED90.VDD, RGB_SMD_LED90.VSS, RGB_SMD_LED91.NC, RGB_SMD_LED91.VDD, RGB_SMD_LED91.VSS, RGB_SMD_LED93.NC, RGB_SMD_LED93.VDD, RGB_SMD_LED93.VSS, RGB_SMD_LED95.NC, RGB_SMD_LED95.VDD, RGB_SMD_LED95.VSS, Q4.E
  N69: RGB_SMD_LED69.DOut, RGB_SMD_LED70.DOut
  N70: RGB_SMD_LED69.DIn, RGB_SMD_LED70.DIn
  VCC_35: RGB_SMD_LED69.VCC, RGB_SMD_LED70.VCC
  N71: RGB_SMD_LED71.DOut, RGB_SMD_LED72.DOut
  N72: RGB_SMD_LED71.DIn, RGB_SMD_LED72.DIn
  VCC_36: RGB_SMD_LED71.VCC, RGB_SMD_LED72.VCC
  N73: RGB_SMD_LED73.DOut, RGB_SMD_LED76.DOut
  N74: RGB_SMD_LED73.DIn, RGB_SMD_LED76.DIn
  VCC_37: RGB_SMD_LED73.VCC, RGB_SMD_LED76.VCC
  N75: RGB_SMD_LED74.DOut, RGB_SMD_LED75.DOut
  N76: RGB_SMD_LED74.DIn, RGB_SMD_LED75.DIn
  VCC_38: RGB_SMD_LED74.VCC, RGB_SMD_LED75.VCC
  N77: RGB_SMD_LED77.DOut, RGB_SMD_LED78.DOut
  N78: RGB_SMD_LED77.DIn, RGB_SMD_LED78.DIn
  VCC_39: RGB_SMD_LED77.VCC, RGB_SMD_LED78.VCC
  N79: RGB_SMD_LED79.DOut, RGB_SMD_LED80.DOut
  N80: RGB_SMD_LED79.DIn, RGB_SMD_LED80.DIn
  VCC_40: RGB_SMD_LED79.VCC, RGB_SMD_LED80.VCC
  N81: RGB_SMD_LED81.DOut, RGB_SMD_LED82.DOut
  N82: RGB_SMD_LED81.DIn, RGB_SMD_LED82.DIn
  VCC_41: RGB_SMD_LED81.VCC, RGB_SMD_LED82.VCC
  N83: RGB_SMD_LED83.DOut, RGB_SMD_LED84.DOut
  N84: RGB_SMD_LED83.DIn, RGB_SMD_LED84.DIn
  VCC_42: RGB_SMD_LED83.VCC, RGB_SMD_LED84.VCC
  N85: RGB_SMD_LED85.DOut, RGB_SMD_LED86.DOut
  N86: RGB_SMD_LED85.DIn, RGB_SMD_LED86.DIn
  VCC_43: RGB_SMD_LED85.VCC, RGB_SMD_LED86.VCC
  N87: RGB_SMD_LED87.DOut, RGB_SMD_LED88.DOut
  N88: RGB_SMD_LED87.DIn, RGB_SMD_LED88.DIn
  VCC_44: RGB_SMD_LED87.VCC, RGB_SMD_LED88.VCC
  N89: RGB_SMD_LED89.DOut, RGB_SMD_LED91.DOut
  N90: RGB_SMD_LED89.DIn, RGB_SMD_LED91.DIn
  VCC_45: RGB_SMD_LED89.VCC, RGB_SMD_LED91.VCC
  N91: RGB_SMD_LED90.DOut, RGB_SMD_LED92.DOut
  N92: RGB_SMD_LED90.DIn, RGB_SMD_LED92.DIn
  VCC_46: RGB_SMD_LED90.VCC, RGB_SMD_LED92.VCC
  N93: RGB_SMD_LED93.DOut, RGB_SMD_LED96.DOut
  N94: RGB_SMD_LED93.DIn, RGB_SMD_LED96.DIn
  VCC_47: RGB_SMD_LED93.VCC, RGB_SMD_LED96.VCC
  N95: RGB_SMD_LED94.DOut, RGB_SMD_LED95.DOut
  N96: RGB_SMD_LED94.DIn, RGB_SMD_LED95.DIn
  VCC_48: RGB_SMD_LED94.VCC, RGB_SMD_LED95.VCC
  N97: RGB_SMD_LED97.DOut, RGB_SMD_LED103.DOut
  N98: RGB_SMD_LED97.DIn, RGB_SMD_LED103.DIn
  VCC_49: RGB_SMD_LED97.VCC, RGB_SMD_LED103.VCC
  VDD_7: RGB_SMD_LED97.NC, RGB_SMD_LED97.VDD, RGB_SMD_LED97.VSS, RGB_SMD_LED100.NC, RGB_SMD_LED100.VDD, RGB_SMD_LED100.VSS, RGB_SMD_LED105.NC, RGB_SMD_LED105.VDD, RGB_SMD_LED105.VSS, RGB_SMD_LED109.NC, RGB_SMD_LED109.VDD, RGB_SMD_LED109.VSS, RGB_SMD_LED113.NC, RGB_SMD_LED113.VDD, RGB_SMD_LED113.VSS, RGB_SMD_LED117.NC, RGB_SMD_LED117.VDD, RGB_SMD_LED117.VSS, RGB_SMD_LED121.NC, RGB_SMD_LED121.VDD, RGB_SMD_LED121.VSS, RGB_SMD_LED128.NC, RGB_SMD_LED128.VDD, RGB_SMD_LED128.VSS, RGB_SMD_LED132.NC, RGB_SMD_LED132.VDD, RGB_SMD_LED132.VSS, RGB_SMD_LED135.NC, RGB_SMD_LED135.VDD, RGB_SMD_LED135.VSS, RGB_SMD_LED138.NC, RGB_SMD_LED138.VDD, RGB_SMD_LED138.VSS, RGB_SMD_LED141.NC, RGB_SMD_LED141.VDD, RGB_SMD_LED141.VSS, RGB_SMD_LED146.NC, RGB_SMD_LED146.VDD, RGB_SMD_LED146.VSS, RGB_SMD_LED152.NC, RGB_SMD_LED152.VDD, RGB_SMD_LED152.VSS, RGB_SMD_LED155.NC, RGB_SMD_LED155.VDD, RGB_SMD_LED155.VSS, RGB_SMD_LED160.NC, RGB_SMD_LED160.VDD, RGB_SMD_LED160.VSS, Q9.E
  N99: RGB_SMD_LED98.DOut, RGB_SMD_LED104.DOut
  N100: RGB_SMD_LED98.DIn, RGB_SMD_LED104.DIn
  VCC_50: RGB_SMD_LED98.VCC, RGB_SMD_LED104.VCC
  VDD_8: RGB_SMD_LED98.NC, RGB_SMD_LED98.VDD, RGB_SMD_LED98.VSS, RGB_SMD_LED99.NC, RGB_SMD_LED99.VDD, RGB_SMD_LED99.VSS, RGB_SMD_LED106.NC, RGB_SMD_LED106.VDD, RGB_SMD_LED106.VSS, RGB_SMD_LED110.NC, RGB_SMD_LED110.VDD, RGB_SMD_LED110.VSS, RGB_SMD_LED114.NC, RGB_SMD_LED114.VDD, RGB_SMD_LED114.VSS, RGB_SMD_LED118.NC, RGB_SMD_LED118.VDD, RGB_SMD_LED118.VSS, RGB_SMD_LED122.NC, RGB_SMD_LED122.VDD, RGB_SMD_LED122.VSS, RGB_SMD_LED127.NC, RGB_SMD_LED127.VDD, RGB_SMD_LED127.VSS, RGB_SMD_LED131.NC, RGB_SMD_LED131.VDD, RGB_SMD_LED131.VSS, RGB_SMD_LED136.NC, RGB_SMD_LED136.VDD, RGB_SMD_LED136.VSS, RGB_SMD_LED137.NC, RGB_SMD_LED137.VDD, RGB_SMD_LED137.VSS, RGB_SMD_LED142.NC, RGB_SMD_LED142.VDD, RGB_SMD_LED142.VSS, RGB_SMD_LED145.NC, RGB_SMD_LED145.VDD, RGB_SMD_LED145.VSS, RGB_SMD_LED151.NC, RGB_SMD_LED151.VDD, RGB_SMD_LED151.VSS, RGB_SMD_LED156.NC, RGB_SMD_LED156.VDD, RGB_SMD_LED156.VSS, RGB_SMD_LED159.NC, RGB_SMD_LED159.VDD, RGB_SMD_LED159.VSS, Q7.E
  N101: RGB_SMD_LED99.DOut, RGB_SMD_LED102.DOut
  N102: RGB_SMD_LED99.DIn, RGB_SMD_LED102.DIn
  VCC_51: RGB_SMD_LED99.VCC, RGB_SMD_LED102.VCC
  N103: RGB_SMD_LED100.DOut, RGB_SMD_LED101.DOut
  N104: RGB_SMD_LED100.DIn, RGB_SMD_LED101.DIn
  VCC_52: RGB_SMD_LED100.VCC, RGB_SMD_LED101.VCC
  VDD_9: RGB_SMD_LED101.NC, RGB_SMD_LED101.VDD, RGB_SMD_LED101.VSS, RGB_SMD_LED103.NC, RGB_SMD_LED103.VDD, RGB_SMD_LED103.VSS, RGB_SMD_LED107.NC, RGB_SMD_LED107.VDD, RGB_SMD_LED107.VSS, RGB_SMD_LED112.NC, RGB_SMD_LED112.VDD, RGB_SMD_LED112.VSS, RGB_SMD_LED116.NC, RGB_SMD_LED116.VDD, RGB_SMD_LED116.VSS, RGB_SMD_LED119.NC, RGB_SMD_LED119.VDD, RGB_SMD_LED119.VSS, RGB_SMD_LED124.NC, RGB_SMD_LED124.VDD, RGB_SMD_LED124.VSS, RGB_SMD_LED126.NC, RGB_SMD_LED126.VDD, RGB_SMD_LED126.VSS, RGB_SMD_LED129.NC, RGB_SMD_LED129.VDD, RGB_SMD_LED129.VSS, RGB_SMD_LED133.NC, RGB_SMD_LED133.VDD, RGB_SMD_LED133.VSS, RGB_SMD_LED139.NC, RGB_SMD_LED139.VDD, RGB_SMD_LED139.VSS, RGB_SMD_LED143.NC, RGB_SMD_LED143.VDD, RGB_SMD_LED143.VSS, RGB_SMD_LED148.NC, RGB_SMD_LED148.VDD, RGB_SMD_LED148.VSS, RGB_SMD_LED150.NC, RGB_SMD_LED150.VDD, RGB_SMD_LED150.VSS, RGB_SMD_LED154.NC, RGB_SMD_LED154.VDD, RGB_SMD_LED154.VSS, RGB_SMD_LED158.NC, RGB_SMD_LED158.VDD, RGB_SMD_LED158.VSS, Q8.E
  VDD_10: RGB_SMD_LED102.NC, RGB_SMD_LED102.VDD, RGB_SMD_LED102.VSS, RGB_SMD_LED104.NC, RGB_SMD_LED104.VDD, RGB_SMD_LED104.VSS, RGB_SMD_LED108.NC, RGB_SMD_LED108.VDD, RGB_SMD_LED108.VSS, RGB_SMD_LED111.NC, RGB_SMD_LED111.VDD, RGB_SMD_LED111.VSS, RGB_SMD_LED115.NC, RGB_SMD_LED115.VDD, RGB_SMD_LED115.VSS, RGB_SMD_LED120.NC, RGB_SMD_LED120.VDD, RGB_SMD_LED120.VSS, RGB_SMD_LED123.NC, RGB_SMD_LED123.VDD, RGB_SMD_LED123.VSS, RGB_SMD_LED125.NC, RGB_SMD_LED125.VDD, RGB_SMD_LED125.VSS, RGB_SMD_LED130.NC, RGB_SMD_LED130.VDD, RGB_SMD_LED130.VSS, RGB_SMD_LED134.NC, RGB_SMD_LED134.VDD, RGB_SMD_LED134.VSS, RGB_SMD_LED140.NC, RGB_SMD_LED140.VDD, RGB_SMD_LED140.VSS, RGB_SMD_LED144.NC, RGB_SMD_LED144.VDD, RGB_SMD_LED144.VSS, RGB_SMD_LED147.NC, RGB_SMD_LED147.VDD, RGB_SMD_LED147.VSS, RGB_SMD_LED149.NC, RGB_SMD_LED149.VDD, RGB_SMD_LED149.VSS, RGB_SMD_LED153.NC, RGB_SMD_LED153.VDD, RGB_SMD_LED153.VSS, RGB_SMD_LED157.NC, RGB_SMD_LED157.VDD, RGB_SMD_LED157.VSS, Q6.E
  N105: RGB_SMD_LED105.DOut, RGB_SMD_LED107.DOut
  N106: RGB_SMD_LED105.DIn, RGB_SMD_LED107.DIn
  VCC_53: RGB_SMD_LED105.VCC, RGB_SMD_LED107.VCC
  N107: RGB_SMD_LED106.DOut, RGB_SMD_LED108.DOut
  N108: RGB_SMD_LED106.DIn, RGB_SMD_LED108.DIn
  VCC_54: RGB_SMD_LED106.VCC, RGB_SMD_LED108.VCC
  N109: RGB_SMD_LED109.DOut, RGB_SMD_LED112.DOut
  N110: RGB_SMD_LED109.DIn, RGB_SMD_LED112.DIn
  VCC_55: RGB_SMD_LED109.VCC, RGB_SMD_LED112.VCC
  N111: RGB_SMD_LED110.DOut, RGB_SMD_LED111.DOut
  N112: RGB_SMD_LED110.DIn, RGB_SMD_LED111.DIn
  VCC_56: RGB_SMD_LED110.VCC, RGB_SMD_LED111.VCC
  N113: RGB_SMD_LED113.DOut, RGB_SMD_LED119.DOut
  N114: RGB_SMD_LED113.DIn, RGB_SMD_LED119.DIn
  VCC_57: RGB_SMD_LED113.VCC, RGB_SMD_LED119.VCC
  N115: RGB_SMD_LED114.DOut, RGB_SMD_LED120.DOut
  N116: RGB_SMD_LED114.DIn, RGB_SMD_LED120.DIn
  VCC_58: RGB_SMD_LED114.VCC, RGB_SMD_LED120.VCC
  N117: RGB_SMD_LED115.DOut, RGB_SMD_LED118.DOut
  N118: RGB_SMD_LED115.DIn, RGB_SMD_LED118.DIn
  VCC_59: RGB_SMD_LED115.VCC, RGB_SMD_LED118.VCC
  N119: RGB_SMD_LED116.DOut, RGB_SMD_LED117.DOut
  N120: RGB_SMD_LED116.DIn, RGB_SMD_LED117.DIn
  VCC_60: RGB_SMD_LED116.VCC, RGB_SMD_LED117.VCC
  N121: RGB_SMD_LED121.DOut, RGB_SMD_LED124.DOut
  N122: RGB_SMD_LED121.DIn, RGB_SMD_LED124.DIn
  VCC_61: RGB_SMD_LED121.VCC, RGB_SMD_LED124.VCC
  N123: RGB_SMD_LED122.DOut, RGB_SMD_LED123.DOut
  N124: RGB_SMD_LED122.DIn, RGB_SMD_LED123.DIn
  VCC_62: RGB_SMD_LED122.VCC, RGB_SMD_LED123.VCC
  N125: RGB_SMD_LED125.DOut, RGB_SMD_LED127.DOut
  N126: RGB_SMD_LED125.DIn, RGB_SMD_LED127.DIn
  VCC_63: RGB_SMD_LED125.VCC, RGB_SMD_LED127.VCC
  N127: RGB_SMD_LED126.DOut, RGB_SMD_LED128.DOut
  N128: RGB_SMD_LED126.DIn, RGB_SMD_LED128.DIn
  VCC_64: RGB_SMD_LED126.VCC, RGB_SMD_LED128.VCC
  N129: RGB_SMD_LED129.DOut, RGB_SMD_LED132.DOut
  N130: RGB_SMD_LED129.DIn, RGB_SMD_LED132.DIn
  VCC_65: RGB_SMD_LED129.VCC, RGB_SMD_LED132.VCC
  N131: RGB_SMD_LED130.DOut, RGB_SMD_LED131.DOut
  N132: RGB_SMD_LED130.DIn, RGB_SMD_LED131.DIn
  VCC_66: RGB_SMD_LED130.VCC, RGB_SMD_LED131.VCC
  N133: RGB_SMD_LED133.DOut, RGB_SMD_LED135.DOut
  N134: RGB_SMD_LED133.DIn, RGB_SMD_LED135.DIn
  VCC_67: RGB_SMD_LED133.VCC, RGB_SMD_LED135.VCC
  N135: RGB_SMD_LED134.DOut, RGB_SMD_LED136.DOut
  N136: RGB_SMD_LED134.DIn, RGB_SMD_LED136.DIn
  VCC_68: RGB_SMD_LED134.VCC, RGB_SMD_LED136.VCC
  N137: RGB_SMD_LED137.DOut, RGB_SMD_LED140.DOut
  N138: RGB_SMD_LED137.DIn, RGB_SMD_LED140.DIn
  VCC_69: RGB_SMD_LED137.VCC, RGB_SMD_LED140.VCC
  N139: RGB_SMD_LED138.DOut, RGB_SMD_LED139.DOut
  N140: RGB_SMD_LED138.DIn, RGB_SMD_LED139.DIn
  VCC_70: RGB_SMD_LED138.VCC, RGB_SMD_LED139.VCC
  N141: RGB_SMD_LED141.DOut, RGB_SMD_LED143.DOut
  N142: RGB_SMD_LED141.DIn, RGB_SMD_LED143.DIn
  VCC_71: RGB_SMD_LED141.VCC, RGB_SMD_LED143.VCC
  N143: RGB_SMD_LED142.DOut, RGB_SMD_LED144.DOut
  N144: RGB_SMD_LED142.DIn, RGB_SMD_LED144.DIn
  VCC_72: RGB_SMD_LED142.VCC, RGB_SMD_LED144.VCC
  N145: RGB_SMD_LED145.DOut, RGB_SMD_LED149.DOut
  N146: RGB_SMD_LED145.DIn, RGB_SMD_LED149.DIn
  VCC_73: RGB_SMD_LED145.VCC, RGB_SMD_LED149.VCC
  N147: RGB_SMD_LED146.DOut, RGB_SMD_LED150.DOut
  N148: RGB_SMD_LED146.DIn, RGB_SMD_LED150.DIn
  VCC_74: RGB_SMD_LED146.VCC, RGB_SMD_LED150.VCC
  N149: RGB_SMD_LED147.DOut, RGB_SMD_LED151.DOut
  N150: RGB_SMD_LED147.DIn, RGB_SMD_LED151.DIn
  VCC_75: RGB_SMD_LED147.VCC, RGB_SMD_LED151.VCC
  N151: RGB_SMD_LED148.DOut, RGB_SMD_LED152.DOut
  N152: RGB_SMD_LED148.DIn, RGB_SMD_LED152.DIn
  VCC_76: RGB_SMD_LED148.VCC, RGB_SMD_LED152.VCC
  N153: RGB_SMD_LED153.DOut, RGB_SMD_LED159.DOut
  N154: RGB_SMD_LED153.DIn, RGB_SMD_LED159.DIn
  VCC_77: RGB_SMD_LED153.VCC, RGB_SMD_LED159.VCC
  N155: RGB_SMD_LED154.DOut, RGB_SMD_LED160.DOut
  N156: RGB_SMD_LED154.DIn, RGB_SMD_LED160.DIn
  VCC_78: RGB_SMD_LED154.VCC, RGB_SMD_LED160.VCC
  N157: RGB_SMD_LED155.DOut, RGB_SMD_LED158.DOut
  N158: RGB_SMD_LED155.DIn, RGB_SMD_LED158.DIn
  VCC_79: RGB_SMD_LED155.VCC, RGB_SMD_LED158.VCC
  N159: RGB_SMD_LED156.DOut, RGB_SMD_LED157.DOut
  N160: RGB_SMD_LED156.DIn, RGB_SMD_LED157.DIn
  VCC_80: RGB_SMD_LED156.VCC, RGB_SMD_LED157.VCC
  VDD_11: RGB_SMD_LED161.NC, RGB_SMD_LED161.VDD, RGB_SMD_LED161.VSS, RGB_SMD_LED162.NC, RGB_SMD_LED162.VDD, RGB_SMD_LED162.VSS, RGB_SMD_LED163.NC, RGB_SMD_LED163.VDD, RGB_SMD_LED163.VSS, RGB_SMD_LED164.NC, RGB_SMD_LED164.VDD, RGB_SMD_LED164.VSS, RGB_SMD_LED165.NC, RGB_SMD_LED165.VDD, RGB_SMD_LED165.VSS, RGB_SMD_LED166.NC, RGB_SMD_LED166.VDD, RGB_SMD_LED166.VSS, RGB_SMD_LED167.NC, RGB_SMD_LED167.VDD, RGB_SMD_LED167.VSS, RGB_SMD_LED168.NC, RGB_SMD_LED168.VDD, RGB_SMD_LED168.VSS, RGB_SMD_LED169.NC, RGB_SMD_LED169.VDD, RGB_SMD_LED169.VSS, RGB_SMD_LED170.NC, RGB_SMD_LED170.VDD, RGB_SMD_LED170.VSS, RGB_SMD_LED171.NC, RGB_SMD_LED171.VDD, RGB_SMD_LED171.VSS, RGB_SMD_LED172.NC, RGB_SMD_LED172.VDD, RGB_SMD_LED172.VSS, RGB_SMD_LED173.NC, RGB_SMD_LED173.VDD, RGB_SMD_LED173.VSS, RGB_SMD_LED174.NC, RGB_SMD_LED174.VDD, RGB_SMD_LED174.VSS, RGB_SMD_LED175.NC, RGB_SMD_LED175.VDD, RGB_SMD_LED175.VSS, RGB_SMD_LED176.NC, RGB_SMD_LED176.VDD, RGB_SMD_LED176.VSS, Q10.E
  N161: Q1.B, ATMega328.D8
  VDD_12: Q1.C, Q2.C, Q3.C, Q4.C, Q5.C, Q6.C, Q7.C, Q8.C, Q9.C, Q10.C, Q11.C, ATMega328.VCC, PCA9956B_Addr_0x32.AD0, PCA9956B_Addr_0x32.AD1, PCA9956B_Addr_0x32.Vdd, PCA9956B_Addr_0x2A.AD1, PCA9956B_Addr_0x2A.Vdd, C3.1, R7_10kOhm.Pin_1, R8_10kOhm.Pin_1, R6_10kOhm.Pin_1, R4_10kOhm.Pin_1, R1_10kOhm.Pin_0, R2_10kOhm.Pin_0, S3.leg1, D1.C
  N162: Q2.B, ATMega328.D7
  N163: Q3.B, ATMega328.D6_(PWM)
  N164: Q4.B, ATMega328.D5_(PWM)
  N165: Q5.B, ATMega328.XLAT2
  N166: Q6.B, ATMega328.XLAT1
  N167: Q7.B, ATMega328.D4
  N168: Q8.B, ATMega328.D3_(PWM)
  N169: Q9.B, ATMega328.D2
  N170: Q10.B, ATMega328.D1_(TX)
  N171: Q11.B, ATMega328.D0_(RX)
  GND: ATMega328.GND, MCP7940M_Addr_0xDE.pin4, PCA9956B_Addr_0x32.AD2, PCA9956B_Addr_0x32.~OE, PCA9956B_Addr_0x32.Vss, PCA9956B_Addr_0x2A.AD0, PCA9956B_Addr_0x2A.AD2, PCA9956B_Addr_0x2A.~OE, PCA9956B_Addr_0x2A.Vss, C3.2, C2.2, C1.2, S1.leg0, S2.leg0, R5_3kOhm.Pin_1, R3_3kOhm.Pin_1, C5_0_1uF.2, C4_0_1uF.2, X1.GND, +_Batt_-.2
  N172: ATMega328.D9_(PWM), S2.leg1, R8_10kOhm.Pin_0, C5_0_1uF.1
  N173: ATMega328.D10_(PWM), S1.leg1, R7_10kOhm.Pin_0, C4_0_1uF.1
  N174: ATMega328.A4, MCP7940M_Addr_0xDE.pin5, PCA9956B_Addr_0x32.SDA, PCA9956B_Addr_0x2A.SDA, R2_10kOhm.Pin_1
  N175: ATMega328.A5, MCP7940M_Addr_0xDE.pin6, PCA9956B_Addr_0x32.SCL, PCA9956B_Addr_0x2A.SCL, R1_10kOhm.Pin_1
  N176: MCP7940M_Addr_0xDE.pin1, XTAL_32_768kHz.X1, C1.1
  N177: MCP7940M_Addr_0xDE.pin2, XTAL_32_768kHz.X2, C2.1
  N178: MCP7940M_Addr_0xDE.pin8, D1.A, +_Batt_-.1
  N179: PCA9956B_Addr_0x32.REXT, R3_3kOhm.Pin_0
  N180: PCA9956B_Addr_0x32.~RESET, R4_10kOhm.Pin_0
  N181: PCA9956B_Addr_0x2A.REXT, R5_3kOhm.Pin_0
  N182: PCA9956B_Addr_0x2A.~RESET, R6_10kOhm.Pin_0
  N183: X1.VBUS, S3.leg0
